// Logisim project Processor.circ as structural Verilog: 3 circuits, main circuit main
module main (
);

  ULA ula_1 ();  // open: F2, F1, F0, A, B, C
  Datapath datapath_1 ();  // open: MBR_Data, in_2, in_3, in_4, in_5, in_6, Reset, in_8, in_9, in_10, External_Input, in_11, in_12, External_Output
endmodule

module ULA (
  input  [7:0] A,
  input  F2,
  input  F1,
  input  F0,
  input  [7:0] B,
  output [7:0] C
);

  wire [7:0] adder_1_out, adder_2_out, adder_3_out, and_1_out, or_1_out, subtractor_1_out;

  Adder adder_1 (.a(A), .b(8'h1), .out(adder_1_out));  // open: cin, cout
  Adder adder_2 (.a(B), .b(8'h1), .out(adder_2_out));  // open: cin, cout
  Adder adder_3 (.a(A), .b(B), .out(adder_3_out));  // open: cin, cout
  Subtractor subtractor_1 (.a(A), .b(B), .out(subtractor_1_out));  // open: bin, bout
  assign and_1_out = A & B;  // AND_Gate and_1, 8 bits wide
  assign or_1_out = A | B;  // OR_Gate or_1, 8 bits wide
  Multiplexer #(.select(3), .width(8)) multiplexer_1 (
    .in0(A), .in1(B), .in2(adder_1_out), .in3(adder_2_out), .in4(adder_3_out), .in5(subtractor_1_out),
    .in6(and_1_out), .in7(or_1_out), .out(C), .sel({F2, F1, F0}));  // open: en
endmodule

module Datapath (
  input  [7:0] MBR_Data,
  input  in_2,
  input  in_3,
  input  in_4,
  input  in_5,
  input  in_6,
  input  Reset,
  input  in_8,
  input  in_9,
  input  in_10,
  input  in_11,
  input  in_12,
  input  [7:0] External_Input,
  input  [7:0] External_Output
);

  wire Clock_out;
  wire [7:0] A_q, B_q, MBR_q, multiplexer_1_out, PC_q, ula_1_c;

  Clock Clock (.out(Clock_out));
  Register A (.D(ula_1_c), .en(in_6), .Q(A_q), .clk(Clock_out), .clr(Reset));
  Register B (.D(ula_1_c), .en(in_5), .Q(B_q), .clk(Clock_out), .clr(Reset));
  Register MBR (.D(MBR_Data), .en(in_4), .Q(MBR_q), .clk(Clock_out), .clr(Reset));
  Register PC (.D(ula_1_c), .en(in_3), .Q(PC_q), .clk(Clock_out), .clr(Reset));
  Register OUT (.D(ula_1_c), .en(in_2), .Q(External_Output), .clk(Clock_out), .clr(Reset));
  Multiplexer #(.select(2), .width(8)) multiplexer_1 (
    .in0(B_q), .in1(MBR_q), .in2(PC_q), .in3(External_Input), .out(multiplexer_1_out), .sel({in_11, in_12}),
    .en(1'b1));
  ULA ula_1 (.F2(in_8), .F1(in_9), .F0(in_10), .A(A_q), .B(multiplexer_1_out), .C(ula_1_c));

  // Notes on the sheet:
  //   B Bus Selector
endmodule
